// Logisim project TRABALHO.circ as structural Verilog: 17 circuits, main circuit main
module main (
  output [31:0] Display
);

  wire CLK;
  wire [7:0] Memoria_de_controle_data;
  wire [23:0] multiplexer_1_out, pc_1_pc_atual, somador_pc_1_pc_prox, somador_pc_2_pc_prox, undriven;
  wire [31:0] banco_de_registradores_1_a, banco_de_registradores_1_b, extensor_sinal_16_bits_1_s,
       Memoria_de_instrucoes_data, multiplexer_2_out, multiplexer_3_out, ula_1_s;

  Multiplexer #(.width(24)) multiplexer_1 (
    .in0(somador_pc_1_pc_prox), .in1(somador_pc_2_pc_prox), .out(multiplexer_1_out),
    .sel(Memoria_de_controle_data[7]));
  Somador_PC somador_pc_1 (.PC(pc_1_pc_atual), .Deslocamento(24'h1), .PC_prox(somador_pc_1_pc_prox));
  PC pc_1 (.PC_prox(multiplexer_1_out), .CLK(CLK), .PC_atual(pc_1_pc_atual));
  Clock clock_1 (.out(CLK));
  Somador_PC somador_pc_2 (.PC(pc_1_pc_atual), .Deslocamento(undriven), .PC_prox(somador_pc_2_pc_prox));
  ROM #(.addrWidth(24), .dataWidth(32)) Memoria_de_instrucoes (.addr(pc_1_pc_atual), .data(Memoria_de_instrucoes_data));
  ROM #(.addrWidth(4)) Memoria_de_controle (.addr(Memoria_de_instrucoes_data[31:28]), .data(Memoria_de_controle_data));
  Banco_de_registradores banco_de_registradores_1 (
    .B_end(Memoria_de_instrucoes_data[19:16]), .A_end(Memoria_de_instrucoes_data[23:20]),
    .W(Memoria_de_controle_data[6]), .W_end(Memoria_de_instrucoes_data[27:24]), .Write(multiplexer_3_out),
    .CLK(CLK), .A(banco_de_registradores_1_a), .B(banco_de_registradores_1_b));
  Extensor_sinal_16_bits extensor_sinal_16_bits_1 (
    .Imm(Memoria_de_instrucoes_data[15:0]), .S(extensor_sinal_16_bits_1_s));
  Multiplexer #(.width(32)) multiplexer_2 (
    .in0(banco_de_registradores_1_b), .in1(extensor_sinal_16_bits_1_s), .out(multiplexer_2_out),
    .sel(Memoria_de_controle_data[5]));
  ULA ula_1 (
    .A(banco_de_registradores_1_a), .B(multiplexer_2_out), .Funct(Memoria_de_controle_data[2:0]), .S(ula_1_s));  // open: ZERO
  Multiplexer #(.width(32)) multiplexer_3 (
    .in0(ula_1_s), .in1(extensor_sinal_16_bits_1_s), .out(multiplexer_3_out),
    .sel(Memoria_de_controle_data[4]));
  Multiplexer #(.width(32)) multiplexer_4 (
    .in1(banco_de_registradores_1_a), .out(Display), .sel(Memoria_de_controle_data[3]));  // open: in0

  // Notes on the sheet:
  //   contents of Memoria_de_instrucoes (hex, n*v repeats v):
  //   0 11000000 12000007 13000012 1400000a 15000000 c4500000 46530000 21120000 95500001 d0100000 b0000000
  //   d0100000 e0000000
  //   contents of Memoria_de_controle (hex, n*v repeats v):
  //   0 50 40 41 42 43 44 45 46 60 61 80 81 8 80
endmodule

module PC (
  input  [23:0] PC_prox,
  input  CLK,
  output [23:0] PC_atual
);

  wire multiplexer_1_out, multiplexer_2_out, multiplexer_3_out, multiplexer_4_out, multiplexer_5_out,
       multiplexer_6_out, multiplexer_7_out, multiplexer_8_out, multiplexer_9_out, multiplexer_10_out,
       multiplexer_11_out, multiplexer_12_out, multiplexer_13_out, multiplexer_14_out, multiplexer_15_out,
       multiplexer_16_out, multiplexer_17_out, multiplexer_18_out, multiplexer_19_out, multiplexer_20_out,
       multiplexer_21_out, multiplexer_22_out, multiplexer_23_out, multiplexer_24_out;

  Multiplexer multiplexer_1 (.in0(PC_atual[0]), .in1(PC_prox[0]), .out(multiplexer_1_out), .sel(1'b1));
  Multiplexer multiplexer_2 (.in0(PC_atual[1]), .in1(PC_prox[1]), .out(multiplexer_2_out), .sel(1'b1));
  Multiplexer multiplexer_3 (.in0(PC_atual[2]), .in1(PC_prox[2]), .out(multiplexer_3_out), .sel(1'b1));
  Multiplexer multiplexer_4 (.in0(PC_atual[3]), .in1(PC_prox[3]), .out(multiplexer_4_out), .sel(1'b1));
  Multiplexer multiplexer_5 (.in0(PC_atual[4]), .in1(PC_prox[4]), .out(multiplexer_5_out), .sel(1'b1));
  Multiplexer multiplexer_6 (.in0(PC_atual[5]), .in1(PC_prox[5]), .out(multiplexer_6_out), .sel(1'b1));
  Multiplexer multiplexer_7 (.in0(PC_atual[6]), .in1(PC_prox[6]), .out(multiplexer_7_out), .sel(1'b1));
  Multiplexer multiplexer_8 (.in0(PC_atual[7]), .in1(PC_prox[7]), .out(multiplexer_8_out), .sel(1'b1));
  Multiplexer multiplexer_9 (.in0(PC_atual[8]), .in1(PC_prox[8]), .out(multiplexer_9_out), .sel(1'b1));
  Multiplexer multiplexer_10 (.in0(PC_atual[9]), .in1(PC_prox[9]), .out(multiplexer_10_out), .sel(1'b1));
  Multiplexer multiplexer_11 (.in0(PC_atual[10]), .in1(PC_prox[10]), .out(multiplexer_11_out), .sel(1'b1));
  Multiplexer multiplexer_12 (.in0(PC_atual[11]), .in1(PC_prox[11]), .out(multiplexer_12_out), .sel(1'b1));
  Multiplexer multiplexer_13 (.in0(PC_atual[12]), .in1(PC_prox[12]), .out(multiplexer_13_out), .sel(1'b1));
  Multiplexer multiplexer_14 (.in0(PC_atual[13]), .in1(PC_prox[13]), .out(multiplexer_14_out), .sel(1'b1));
  Multiplexer multiplexer_15 (.in0(PC_atual[14]), .in1(PC_prox[14]), .out(multiplexer_15_out), .sel(1'b1));
  Multiplexer multiplexer_16 (.in0(PC_atual[15]), .in1(PC_prox[15]), .out(multiplexer_16_out), .sel(1'b1));
  Multiplexer multiplexer_17 (.in0(PC_atual[16]), .in1(PC_prox[16]), .out(multiplexer_17_out), .sel(1'b1));
  Multiplexer multiplexer_18 (.in0(PC_atual[17]), .in1(PC_prox[17]), .out(multiplexer_18_out), .sel(1'b1));
  Multiplexer multiplexer_19 (.in0(PC_atual[18]), .in1(PC_prox[18]), .out(multiplexer_19_out), .sel(1'b1));
  Multiplexer multiplexer_20 (.in0(PC_atual[19]), .in1(PC_prox[19]), .out(multiplexer_20_out), .sel(1'b1));
  Multiplexer multiplexer_21 (.in0(PC_atual[20]), .in1(PC_prox[20]), .out(multiplexer_21_out), .sel(1'b1));
  Multiplexer multiplexer_22 (.in0(PC_atual[21]), .in1(PC_prox[21]), .out(multiplexer_22_out), .sel(1'b1));
  Multiplexer multiplexer_23 (.in0(PC_atual[22]), .in1(PC_prox[22]), .out(multiplexer_23_out), .sel(1'b1));
  Multiplexer multiplexer_24 (.in0(PC_atual[23]), .in1(PC_prox[23]), .out(multiplexer_24_out), .sel(1'b1));
  D_Flip_Flop d_ff_1 (.D(multiplexer_1_out), .clk(CLK), .Q(PC_atual[0]));  // open: Qn, preset, reset
  D_Flip_Flop d_ff_2 (.D(multiplexer_2_out), .clk(CLK), .Q(PC_atual[1]));  // open: Qn, preset, reset
  D_Flip_Flop d_ff_3 (.D(multiplexer_3_out), .clk(CLK), .Q(PC_atual[2]));  // open: Qn, preset, reset
  D_Flip_Flop d_ff_4 (.D(multiplexer_4_out), .clk(CLK), .Q(PC_atual[3]));  // open: Qn, preset, reset
  D_Flip_Flop d_ff_5 (.D(multiplexer_5_out), .clk(CLK), .Q(PC_atual[4]));  // open: Qn, preset, reset
  D_Flip_Flop d_ff_6 (.D(multiplexer_6_out), .clk(CLK), .Q(PC_atual[5]));  // open: Qn, preset, reset
  D_Flip_Flop d_ff_7 (.D(multiplexer_7_out), .clk(CLK), .Q(PC_atual[6]));  // open: Qn, preset, reset
  D_Flip_Flop d_ff_8 (.D(multiplexer_8_out), .clk(CLK), .Q(PC_atual[7]));  // open: Qn, preset, reset
  D_Flip_Flop d_ff_9 (.D(multiplexer_9_out), .clk(CLK), .Q(PC_atual[8]));  // open: Qn, preset, reset
  D_Flip_Flop d_ff_10 (.D(multiplexer_10_out), .clk(CLK), .Q(PC_atual[9]));  // open: Qn, preset, reset
  D_Flip_Flop d_ff_11 (.D(multiplexer_11_out), .clk(CLK), .Q(PC_atual[10]));  // open: Qn, preset, reset
  D_Flip_Flop d_ff_12 (.D(multiplexer_12_out), .clk(CLK), .Q(PC_atual[11]));  // open: Qn, preset, reset
  D_Flip_Flop d_ff_13 (.D(multiplexer_13_out), .clk(CLK), .Q(PC_atual[12]));  // open: Qn, preset, reset
  D_Flip_Flop d_ff_14 (.D(multiplexer_14_out), .clk(CLK), .Q(PC_atual[13]));  // open: Qn, preset, reset
  D_Flip_Flop d_ff_15 (.D(multiplexer_15_out), .clk(CLK), .Q(PC_atual[14]));  // open: Qn, preset, reset
  D_Flip_Flop d_ff_16 (.D(multiplexer_16_out), .clk(CLK), .Q(PC_atual[15]));  // open: Qn, preset, reset
  D_Flip_Flop d_ff_17 (.D(multiplexer_17_out), .clk(CLK), .Q(PC_atual[16]));  // open: Qn, preset, reset
  D_Flip_Flop d_ff_18 (.D(multiplexer_18_out), .clk(CLK), .Q(PC_atual[17]));  // open: Qn, preset, reset
  D_Flip_Flop d_ff_19 (.D(multiplexer_19_out), .clk(CLK), .Q(PC_atual[18]));  // open: Qn, preset, reset
  D_Flip_Flop d_ff_20 (.D(multiplexer_20_out), .clk(CLK), .Q(PC_atual[19]));  // open: Qn, preset, reset
  D_Flip_Flop d_ff_21 (.D(multiplexer_21_out), .clk(CLK), .Q(PC_atual[20]));  // open: Qn, preset, reset
  D_Flip_Flop d_ff_22 (.D(multiplexer_22_out), .clk(CLK), .Q(PC_atual[21]));  // open: Qn, preset, reset
  D_Flip_Flop d_ff_23 (.D(multiplexer_23_out), .clk(CLK), .Q(PC_atual[22]));  // open: Qn, preset, reset
  D_Flip_Flop d_ff_24 (.D(multiplexer_24_out), .clk(CLK), .Q(PC_atual[23]));  // open: Qn, preset, reset
endmodule

module Somador_PC (
  input  [23:0] PC,
  input  [23:0] Deslocamento,
  output [23:0] PC_prox
);

  wire somador_8_bits_1_c_out, somador_8_bits_2_c_out;

  Somador_8_bits somador_8_bits_1 (
    .A(PC[7:0]), .B(Deslocamento[7:0]), .C_out(somador_8_bits_1_c_out), .S(PC_prox[7:0]));  // open: C_in
  Somador_8_bits somador_8_bits_2 (
    .A(PC[15:8]), .B(Deslocamento[15:8]), .C_in(somador_8_bits_1_c_out), .C_out(somador_8_bits_2_c_out),
    .S(PC_prox[15:8]));
  Somador_8_bits somador_8_bits_3 (
    .A(PC[23:16]), .B(Deslocamento[23:16]), .C_in(somador_8_bits_2_c_out), .S(PC_prox[23:16]));  // open: C_out
endmodule

module Extensor_sinal_16_bits (
  input  [15:0] Imm,
  output [31:0] S
);


  assign S = {{17{Imm[15]}}, Imm[14:0]};
endmodule

module Registrador_32_bits (
  input  [31:0] a,
  input  W_En,
  input  CLK,
  output [31:0] s
);

  wire multiplexer_1_out, multiplexer_2_out, multiplexer_3_out, multiplexer_4_out, multiplexer_5_out,
       multiplexer_6_out, multiplexer_7_out, multiplexer_8_out, multiplexer_9_out, multiplexer_10_out,
       multiplexer_11_out, multiplexer_12_out, multiplexer_13_out, multiplexer_14_out, multiplexer_15_out,
       multiplexer_16_out, multiplexer_17_out, multiplexer_18_out, multiplexer_19_out, multiplexer_20_out,
       multiplexer_21_out, multiplexer_22_out, multiplexer_23_out, multiplexer_24_out, multiplexer_25_out,
       multiplexer_26_out, multiplexer_27_out, multiplexer_28_out, multiplexer_29_out, multiplexer_30_out,
       multiplexer_31_out, multiplexer_32_out;

  Multiplexer multiplexer_1 (.in0(s[0]), .in1(a[0]), .out(multiplexer_1_out), .sel(W_En));
  Multiplexer multiplexer_2 (.in0(s[1]), .in1(a[1]), .out(multiplexer_2_out), .sel(W_En));
  Multiplexer multiplexer_3 (.in0(s[2]), .in1(a[2]), .out(multiplexer_3_out), .sel(W_En));
  Multiplexer multiplexer_4 (.in0(s[3]), .in1(a[3]), .out(multiplexer_4_out), .sel(W_En));
  Multiplexer multiplexer_5 (.in0(s[4]), .in1(a[4]), .out(multiplexer_5_out), .sel(W_En));
  Multiplexer multiplexer_6 (.in0(s[5]), .in1(a[5]), .out(multiplexer_6_out), .sel(W_En));
  Multiplexer multiplexer_7 (.in0(s[6]), .in1(a[6]), .out(multiplexer_7_out), .sel(W_En));
  Multiplexer multiplexer_8 (.in0(s[7]), .in1(a[7]), .out(multiplexer_8_out), .sel(W_En));
  Multiplexer multiplexer_9 (.in0(s[8]), .in1(a[8]), .out(multiplexer_9_out), .sel(W_En));
  Multiplexer multiplexer_10 (.in0(s[9]), .in1(a[9]), .out(multiplexer_10_out), .sel(W_En));
  Multiplexer multiplexer_11 (.in0(s[10]), .in1(a[10]), .out(multiplexer_11_out), .sel(W_En));
  Multiplexer multiplexer_12 (.in0(s[11]), .in1(a[11]), .out(multiplexer_12_out), .sel(W_En));
  Multiplexer multiplexer_13 (.in0(s[12]), .in1(a[12]), .out(multiplexer_13_out), .sel(W_En));
  Multiplexer multiplexer_14 (.in0(s[13]), .in1(a[13]), .out(multiplexer_14_out), .sel(W_En));
  Multiplexer multiplexer_15 (.in0(s[14]), .in1(a[14]), .out(multiplexer_15_out), .sel(W_En));
  Multiplexer multiplexer_16 (.in0(s[15]), .in1(a[15]), .out(multiplexer_16_out), .sel(W_En));
  Multiplexer multiplexer_17 (.in0(s[16]), .in1(a[16]), .out(multiplexer_17_out), .sel(W_En));
  Multiplexer multiplexer_18 (.in0(s[17]), .in1(a[17]), .out(multiplexer_18_out), .sel(W_En));
  Multiplexer multiplexer_19 (.in0(s[18]), .in1(a[18]), .out(multiplexer_19_out), .sel(W_En));
  Multiplexer multiplexer_20 (.in0(s[19]), .in1(a[19]), .out(multiplexer_20_out), .sel(W_En));
  Multiplexer multiplexer_21 (.in0(s[20]), .in1(a[20]), .out(multiplexer_21_out), .sel(W_En));
  Multiplexer multiplexer_22 (.in0(s[21]), .in1(a[21]), .out(multiplexer_22_out), .sel(W_En));
  Multiplexer multiplexer_23 (.in0(s[22]), .in1(a[22]), .out(multiplexer_23_out), .sel(W_En));
  Multiplexer multiplexer_24 (.in0(s[23]), .in1(a[23]), .out(multiplexer_24_out), .sel(W_En));
  Multiplexer multiplexer_25 (.in0(s[24]), .in1(a[24]), .out(multiplexer_25_out), .sel(W_En));
  Multiplexer multiplexer_26 (.in0(s[25]), .in1(a[25]), .out(multiplexer_26_out), .sel(W_En));
  Multiplexer multiplexer_27 (.in0(s[26]), .in1(a[26]), .out(multiplexer_27_out), .sel(W_En));
  Multiplexer multiplexer_28 (.in0(s[27]), .in1(a[27]), .out(multiplexer_28_out), .sel(W_En));
  Multiplexer multiplexer_29 (.in0(s[28]), .in1(a[28]), .out(multiplexer_29_out), .sel(W_En));
  Multiplexer multiplexer_30 (.in0(s[29]), .in1(a[29]), .out(multiplexer_30_out), .sel(W_En));
  Multiplexer multiplexer_31 (.in0(s[30]), .in1(a[30]), .out(multiplexer_31_out), .sel(W_En));
  Multiplexer multiplexer_32 (.in0(s[31]), .in1(a[31]), .out(multiplexer_32_out), .sel(W_En));
  D_Flip_Flop d_ff_1 (.D(multiplexer_1_out), .clk(CLK), .Q(s[0]));  // open: Qn, preset, reset
  D_Flip_Flop d_ff_2 (.D(multiplexer_2_out), .clk(CLK), .Q(s[1]));  // open: Qn, preset, reset
  D_Flip_Flop d_ff_3 (.D(multiplexer_3_out), .clk(CLK), .Q(s[2]));  // open: Qn, preset, reset
  D_Flip_Flop d_ff_4 (.D(multiplexer_4_out), .clk(CLK), .Q(s[3]));  // open: Qn, preset, reset
  D_Flip_Flop d_ff_5 (.D(multiplexer_5_out), .clk(CLK), .Q(s[4]));  // open: Qn, preset, reset
  D_Flip_Flop d_ff_6 (.D(multiplexer_6_out), .clk(CLK), .Q(s[5]));  // open: Qn, preset, reset
  D_Flip_Flop d_ff_7 (.D(multiplexer_7_out), .clk(CLK), .Q(s[6]));  // open: Qn, preset, reset
  D_Flip_Flop d_ff_8 (.D(multiplexer_8_out), .clk(CLK), .Q(s[7]));  // open: Qn, preset, reset
  D_Flip_Flop d_ff_9 (.D(multiplexer_9_out), .clk(CLK), .Q(s[8]));  // open: Qn, preset, reset
  D_Flip_Flop d_ff_10 (.D(multiplexer_10_out), .clk(CLK), .Q(s[9]));  // open: Qn, preset, reset
  D_Flip_Flop d_ff_11 (.D(multiplexer_11_out), .clk(CLK), .Q(s[10]));  // open: Qn, preset, reset
  D_Flip_Flop d_ff_12 (.D(multiplexer_12_out), .clk(CLK), .Q(s[11]));  // open: Qn, preset, reset
  D_Flip_Flop d_ff_13 (.D(multiplexer_13_out), .clk(CLK), .Q(s[12]));  // open: Qn, preset, reset
  D_Flip_Flop d_ff_14 (.D(multiplexer_14_out), .clk(CLK), .Q(s[13]));  // open: Qn, preset, reset
  D_Flip_Flop d_ff_15 (.D(multiplexer_15_out), .clk(CLK), .Q(s[14]));  // open: Qn, preset, reset
  D_Flip_Flop d_ff_16 (.D(multiplexer_16_out), .clk(CLK), .Q(s[15]));  // open: Qn, preset, reset
  D_Flip_Flop d_ff_17 (.D(multiplexer_17_out), .clk(CLK), .Q(s[16]));  // open: Qn, preset, reset
  D_Flip_Flop d_ff_18 (.D(multiplexer_18_out), .clk(CLK), .Q(s[17]));  // open: Qn, preset, reset
  D_Flip_Flop d_ff_19 (.D(multiplexer_19_out), .clk(CLK), .Q(s[18]));  // open: Qn, preset, reset
  D_Flip_Flop d_ff_20 (.D(multiplexer_20_out), .clk(CLK), .Q(s[19]));  // open: Qn, preset, reset
  D_Flip_Flop d_ff_21 (.D(multiplexer_21_out), .clk(CLK), .Q(s[20]));  // open: Qn, preset, reset
  D_Flip_Flop d_ff_22 (.D(multiplexer_22_out), .clk(CLK), .Q(s[21]));  // open: Qn, preset, reset
  D_Flip_Flop d_ff_23 (.D(multiplexer_23_out), .clk(CLK), .Q(s[22]));  // open: Qn, preset, reset
  D_Flip_Flop d_ff_24 (.D(multiplexer_24_out), .clk(CLK), .Q(s[23]));  // open: Qn, preset, reset
  D_Flip_Flop d_ff_25 (.D(multiplexer_25_out), .clk(CLK), .Q(s[24]));  // open: Qn, preset, reset
  D_Flip_Flop d_ff_26 (.D(multiplexer_26_out), .clk(CLK), .Q(s[25]));  // open: Qn, preset, reset
  D_Flip_Flop d_ff_27 (.D(multiplexer_27_out), .clk(CLK), .Q(s[26]));  // open: Qn, preset, reset
  D_Flip_Flop d_ff_28 (.D(multiplexer_28_out), .clk(CLK), .Q(s[27]));  // open: Qn, preset, reset
  D_Flip_Flop d_ff_29 (.D(multiplexer_29_out), .clk(CLK), .Q(s[28]));  // open: Qn, preset, reset
  D_Flip_Flop d_ff_30 (.D(multiplexer_30_out), .clk(CLK), .Q(s[29]));  // open: Qn, preset, reset
  D_Flip_Flop d_ff_31 (.D(multiplexer_31_out), .clk(CLK), .Q(s[30]));  // open: Qn, preset, reset
  D_Flip_Flop d_ff_32 (.D(multiplexer_32_out), .clk(CLK), .Q(s[31]));  // open: Qn, preset, reset
endmodule

module Banco_de_registradores (
  input  W,
  input  CLK,
  input  [31:0] Write,
  input  [3:0] W_end,
  input  [3:0] B_end,
  input  [3:0] A_end,
  output [31:0] A,
  output [31:0] B
);

  wire demultiplexer_1_out1, demultiplexer_1_out2, demultiplexer_1_out3, demultiplexer_1_out4,
       demultiplexer_1_out5, demultiplexer_1_out6, demultiplexer_1_out7, demultiplexer_1_out8,
       demultiplexer_1_out9, demultiplexer_1_out10, demultiplexer_1_out11, demultiplexer_1_out12,
       demultiplexer_1_out13, demultiplexer_1_out14, demultiplexer_1_out15;
  wire [31:0] registrador_32_bits_1_s, registrador_32_bits_2_s, registrador_32_bits_3_s,
       registrador_32_bits_4_s, registrador_32_bits_5_s, registrador_32_bits_6_s, registrador_32_bits_7_s,
       registrador_32_bits_8_s, registrador_32_bits_9_s, registrador_32_bits_10_s, registrador_32_bits_11_s,
       registrador_32_bits_12_s, registrador_32_bits_13_s, registrador_32_bits_14_s,
       registrador_32_bits_15_s, registrador_32_bits_16_s;

  Demultiplexer #(.select(4)) demultiplexer_1 (
    .out1(demultiplexer_1_out1), .out2(demultiplexer_1_out2), .out3(demultiplexer_1_out3),
    .out4(demultiplexer_1_out4), .out5(demultiplexer_1_out5), .out6(demultiplexer_1_out6),
    .out7(demultiplexer_1_out7), .out8(demultiplexer_1_out8), .out9(demultiplexer_1_out9),
    .out10(demultiplexer_1_out10), .out11(demultiplexer_1_out11), .out12(demultiplexer_1_out12),
    .out13(demultiplexer_1_out13), .out14(demultiplexer_1_out14), .out15(demultiplexer_1_out15), .in(W),
    .sel(W_end));  // open: out0
  Registrador_32_bits registrador_32_bits_1 (.a(Write), .CLK(CLK), .s(registrador_32_bits_1_s));  // open: W_En
  Registrador_32_bits registrador_32_bits_2 (
    .a(Write), .W_En(demultiplexer_1_out1), .CLK(CLK), .s(registrador_32_bits_2_s));
  Registrador_32_bits registrador_32_bits_3 (
    .a(Write), .W_En(demultiplexer_1_out2), .CLK(CLK), .s(registrador_32_bits_3_s));
  Registrador_32_bits registrador_32_bits_4 (
    .a(Write), .W_En(demultiplexer_1_out3), .CLK(CLK), .s(registrador_32_bits_4_s));
  Registrador_32_bits registrador_32_bits_5 (
    .a(Write), .W_En(demultiplexer_1_out4), .CLK(CLK), .s(registrador_32_bits_5_s));
  Registrador_32_bits registrador_32_bits_6 (
    .a(Write), .W_En(demultiplexer_1_out5), .CLK(CLK), .s(registrador_32_bits_6_s));
  Registrador_32_bits registrador_32_bits_7 (
    .a(Write), .W_En(demultiplexer_1_out6), .CLK(CLK), .s(registrador_32_bits_7_s));
  Registrador_32_bits registrador_32_bits_8 (
    .a(Write), .W_En(demultiplexer_1_out7), .CLK(CLK), .s(registrador_32_bits_8_s));
  Registrador_32_bits registrador_32_bits_9 (
    .a(Write), .W_En(demultiplexer_1_out8), .CLK(CLK), .s(registrador_32_bits_9_s));
  Registrador_32_bits registrador_32_bits_10 (
    .a(Write), .W_En(demultiplexer_1_out9), .CLK(CLK), .s(registrador_32_bits_10_s));
  Registrador_32_bits registrador_32_bits_11 (
    .a(Write), .W_En(demultiplexer_1_out10), .CLK(CLK), .s(registrador_32_bits_11_s));
  Registrador_32_bits registrador_32_bits_12 (
    .a(Write), .W_En(demultiplexer_1_out11), .CLK(CLK), .s(registrador_32_bits_12_s));
  Registrador_32_bits registrador_32_bits_13 (
    .a(Write), .W_En(demultiplexer_1_out12), .CLK(CLK), .s(registrador_32_bits_13_s));
  Registrador_32_bits registrador_32_bits_14 (
    .a(Write), .W_En(demultiplexer_1_out13), .CLK(CLK), .s(registrador_32_bits_14_s));
  Registrador_32_bits registrador_32_bits_15 (
    .a(Write), .W_En(demultiplexer_1_out14), .CLK(CLK), .s(registrador_32_bits_15_s));
  Registrador_32_bits registrador_32_bits_16 (
    .a(Write), .W_En(demultiplexer_1_out15), .CLK(CLK), .s(registrador_32_bits_16_s));
  Multiplexer #(.select(4), .width(32)) multiplexer_1 (
    .in0(registrador_32_bits_1_s), .in1(registrador_32_bits_2_s), .in2(registrador_32_bits_3_s),
    .in3(registrador_32_bits_4_s), .in4(registrador_32_bits_5_s), .in5(registrador_32_bits_6_s),
    .in6(registrador_32_bits_7_s), .in7(registrador_32_bits_8_s), .in8(registrador_32_bits_9_s),
    .in9(registrador_32_bits_10_s), .in10(registrador_32_bits_11_s), .in11(registrador_32_bits_12_s),
    .in12(registrador_32_bits_13_s), .in13(registrador_32_bits_14_s), .in14(registrador_32_bits_15_s),
    .in15(registrador_32_bits_16_s), .out(A), .sel(A_end));
  Multiplexer #(.select(4), .width(32)) multiplexer_2 (
    .in0(registrador_32_bits_1_s), .in1(registrador_32_bits_2_s), .in2(registrador_32_bits_3_s),
    .in3(registrador_32_bits_4_s), .in4(registrador_32_bits_5_s), .in5(registrador_32_bits_6_s),
    .in6(registrador_32_bits_7_s), .in7(registrador_32_bits_8_s), .in8(registrador_32_bits_9_s),
    .in9(registrador_32_bits_10_s), .in10(registrador_32_bits_11_s), .in11(registrador_32_bits_12_s),
    .in12(registrador_32_bits_13_s), .in13(registrador_32_bits_14_s), .in14(registrador_32_bits_15_s),
    .in15(registrador_32_bits_16_s), .out(B), .sel(B_end));
endmodule

module Full_adder_1_bit (
  input  A,
  input  B,
  input  C_in,
  output S,
  output C_out
);

  wire and_1_out, and_2_out, xor_1_out;

  xor xor_1 (xor_1_out, A, B);
  and and_1 (and_1_out, xor_1_out, C_in);
  and and_2 (and_2_out, B, A);
  xor xor_2 (S, xor_1_out, C_in);
  or or_1 (C_out, and_1_out, and_2_out);
endmodule

module Somador_8_bits (
  input  C_in,
  input  [7:0] A,
  input  [7:0] B,
  output [7:0] S,
  output C_out
);

  wire full_adder_1_bit_1_c_out, full_adder_1_bit_2_c_out, full_adder_1_bit_3_c_out,
       full_adder_1_bit_4_c_out, full_adder_1_bit_5_c_out, full_adder_1_bit_6_c_out, full_adder_1_bit_7_c_out;

  Full_adder_1_bit full_adder_1_bit_1 (.A(A[0]), .B(B[0]), .C_in(C_in), .S(S[0]), .C_out(full_adder_1_bit_1_c_out));
  Full_adder_1_bit full_adder_1_bit_2 (
    .A(A[1]), .B(B[1]), .C_in(full_adder_1_bit_1_c_out), .S(S[1]), .C_out(full_adder_1_bit_2_c_out));
  Full_adder_1_bit full_adder_1_bit_3 (
    .A(A[2]), .B(B[2]), .C_in(full_adder_1_bit_2_c_out), .S(S[2]), .C_out(full_adder_1_bit_3_c_out));
  Full_adder_1_bit full_adder_1_bit_4 (
    .A(A[3]), .B(B[3]), .C_in(full_adder_1_bit_3_c_out), .S(S[3]), .C_out(full_adder_1_bit_4_c_out));
  Full_adder_1_bit full_adder_1_bit_5 (
    .A(A[4]), .B(B[4]), .C_in(full_adder_1_bit_4_c_out), .S(S[4]), .C_out(full_adder_1_bit_5_c_out));
  Full_adder_1_bit full_adder_1_bit_6 (
    .A(A[5]), .B(B[5]), .C_in(full_adder_1_bit_5_c_out), .S(S[5]), .C_out(full_adder_1_bit_6_c_out));
  Full_adder_1_bit full_adder_1_bit_7 (
    .A(A[6]), .B(B[6]), .C_in(full_adder_1_bit_6_c_out), .S(S[6]), .C_out(full_adder_1_bit_7_c_out));
  Full_adder_1_bit full_adder_1_bit_8 (.A(A[7]), .B(B[7]), .C_in(full_adder_1_bit_7_c_out), .S(S[7]), .C_out(C_out));
endmodule

module Somador_32_bits (
  input  C_in,
  input  [31:0] A,
  input  [31:0] B,
  output [31:0] S,
  output Overflow
);

  wire somador_8_bits_1_c_out, somador_8_bits_2_c_out, somador_8_bits_3_c_out;

  Somador_8_bits somador_8_bits_1 (.A(A[7:0]), .B(B[7:0]), .C_in(C_in), .C_out(somador_8_bits_1_c_out), .S(S[7:0]));
  Somador_8_bits somador_8_bits_2 (
    .A(A[15:8]), .B(B[15:8]), .C_in(somador_8_bits_1_c_out), .C_out(somador_8_bits_2_c_out), .S(S[15:8]));
  Somador_8_bits somador_8_bits_3 (
    .A(A[23:16]), .B(B[23:16]), .C_in(somador_8_bits_2_c_out), .C_out(somador_8_bits_3_c_out), .S(S[23:16]));
  Somador_8_bits somador_8_bits_4 (
    .A(A[31:24]), .B(B[31:24]), .C_in(somador_8_bits_3_c_out), .C_out(Overflow), .S(S[31:24]));
endmodule

module Shifter_1_bit (
  input  [31:0] A,
  input  shift,
  output [31:0] S
);

  Multiplexer multiplexer_1 (.in0(A[0]), .in1(1'b0), .out(S[0]), .sel(shift));
  Multiplexer multiplexer_2 (.in0(A[1]), .in1(A[0]), .out(S[1]), .sel(shift));
  Multiplexer multiplexer_3 (.in0(A[2]), .in1(A[1]), .out(S[2]), .sel(shift));
  Multiplexer multiplexer_4 (.in0(A[3]), .in1(A[2]), .out(S[3]), .sel(shift));
  Multiplexer multiplexer_5 (.in0(A[4]), .in1(A[3]), .out(S[4]), .sel(shift));
  Multiplexer multiplexer_6 (.in0(A[5]), .in1(A[4]), .out(S[5]), .sel(shift));
  Multiplexer multiplexer_7 (.in0(A[6]), .in1(A[5]), .out(S[6]), .sel(shift));
  Multiplexer multiplexer_8 (.in0(A[7]), .in1(A[6]), .out(S[7]), .sel(shift));
  Multiplexer multiplexer_9 (.in0(A[8]), .in1(A[7]), .out(S[8]), .sel(shift));
  Multiplexer multiplexer_10 (.in0(A[9]), .in1(A[8]), .out(S[9]), .sel(shift));
  Multiplexer multiplexer_11 (.in0(A[10]), .in1(A[9]), .out(S[10]), .sel(shift));
  Multiplexer multiplexer_12 (.in0(A[11]), .in1(A[10]), .out(S[11]), .sel(shift));
  Multiplexer multiplexer_13 (.in0(A[12]), .in1(A[11]), .out(S[12]), .sel(shift));
  Multiplexer multiplexer_14 (.in0(A[13]), .in1(A[12]), .out(S[13]), .sel(shift));
  Multiplexer multiplexer_15 (.in0(A[14]), .in1(A[13]), .out(S[14]), .sel(shift));
  Multiplexer multiplexer_16 (.in0(A[15]), .in1(A[14]), .out(S[15]), .sel(shift));
  Multiplexer multiplexer_17 (.in0(A[16]), .in1(A[15]), .out(S[16]), .sel(shift));
  Multiplexer multiplexer_18 (.in0(A[17]), .in1(A[16]), .out(S[17]), .sel(shift));
  Multiplexer multiplexer_19 (.in0(A[18]), .in1(A[17]), .out(S[18]), .sel(shift));
  Multiplexer multiplexer_20 (.in0(A[19]), .in1(A[18]), .out(S[19]), .sel(shift));
  Multiplexer multiplexer_21 (.in0(A[20]), .in1(A[19]), .out(S[20]), .sel(shift));
  Multiplexer multiplexer_22 (.in0(A[21]), .in1(A[20]), .out(S[21]), .sel(shift));
  Multiplexer multiplexer_23 (.in0(A[22]), .in1(A[21]), .out(S[22]), .sel(shift));
  Multiplexer multiplexer_24 (.in0(A[23]), .in1(A[22]), .out(S[23]), .sel(shift));
  Multiplexer multiplexer_25 (.in0(A[24]), .in1(A[23]), .out(S[24]), .sel(shift));
  Multiplexer multiplexer_26 (.in0(A[25]), .in1(A[24]), .out(S[25]), .sel(shift));
  Multiplexer multiplexer_27 (.in0(A[26]), .in1(A[25]), .out(S[26]), .sel(shift));
  Multiplexer multiplexer_28 (.in0(A[27]), .in1(A[26]), .out(S[27]), .sel(shift));
  Multiplexer multiplexer_29 (.in0(A[28]), .in1(A[27]), .out(S[28]), .sel(shift));
  Multiplexer multiplexer_30 (.in0(A[29]), .in1(A[28]), .out(S[29]), .sel(shift));
  Multiplexer multiplexer_31 (.in0(A[30]), .in1(A[29]), .out(S[30]), .sel(shift));
  Multiplexer multiplexer_32 (.in0(A[31]), .in1(A[30]), .out(S[31]), .sel(shift));
endmodule

module Shifter_2_bits (
  input  [31:0] A,
  input  shift,
  output [31:0] S
);

  Multiplexer multiplexer_1 (.in0(A[0]), .in1(1'b0), .out(S[0]), .sel(shift));
  Multiplexer multiplexer_2 (.in0(A[1]), .in1(1'b0), .out(S[1]), .sel(shift));
  Multiplexer multiplexer_3 (.in0(A[2]), .in1(A[0]), .out(S[2]), .sel(shift));
  Multiplexer multiplexer_4 (.in0(A[3]), .in1(A[1]), .out(S[3]), .sel(shift));
  Multiplexer multiplexer_5 (.in0(A[4]), .in1(A[2]), .out(S[4]), .sel(shift));
  Multiplexer multiplexer_6 (.in0(A[5]), .in1(A[3]), .out(S[5]), .sel(shift));
  Multiplexer multiplexer_7 (.in0(A[6]), .in1(A[4]), .out(S[6]), .sel(shift));
  Multiplexer multiplexer_8 (.in0(A[7]), .in1(A[5]), .out(S[7]), .sel(shift));
  Multiplexer multiplexer_9 (.in0(A[8]), .in1(A[6]), .out(S[8]), .sel(shift));
  Multiplexer multiplexer_10 (.in0(A[9]), .in1(A[8]), .out(S[9]), .sel(shift));
  Multiplexer multiplexer_11 (.in0(A[10]), .in1(A[9]), .out(S[10]), .sel(shift));
  Multiplexer multiplexer_12 (.in0(A[11]), .in1(A[10]), .out(S[11]), .sel(shift));
  Multiplexer multiplexer_13 (.in0(A[12]), .in1(A[11]), .out(S[12]), .sel(shift));
  Multiplexer multiplexer_14 (.in0(A[13]), .in1(A[12]), .out(S[13]), .sel(shift));
  Multiplexer multiplexer_15 (.in0(A[14]), .in1(A[13]), .out(S[14]), .sel(shift));
  Multiplexer multiplexer_16 (.in0(A[15]), .in1(A[14]), .out(S[15]), .sel(shift));
  Multiplexer multiplexer_17 (.in0(A[16]), .in1(A[15]), .out(S[16]), .sel(shift));
  Multiplexer multiplexer_18 (.in0(A[17]), .in1(A[16]), .out(S[17]), .sel(shift));
  Multiplexer multiplexer_19 (.in0(A[18]), .in1(A[17]), .out(S[18]), .sel(shift));
  Multiplexer multiplexer_20 (.in0(A[19]), .in1(A[18]), .out(S[19]), .sel(shift));
  Multiplexer multiplexer_21 (.in0(A[20]), .in1(A[19]), .out(S[20]), .sel(shift));
  Multiplexer multiplexer_22 (.in0(A[21]), .in1(A[20]), .out(S[21]), .sel(shift));
  Multiplexer multiplexer_23 (.in0(A[22]), .in1(A[21]), .out(S[22]), .sel(shift));
  Multiplexer multiplexer_24 (.in0(A[23]), .in1(A[22]), .out(S[23]), .sel(shift));
  Multiplexer multiplexer_25 (.in0(A[24]), .in1(A[23]), .out(S[24]), .sel(shift));
  Multiplexer multiplexer_26 (.in0(A[25]), .in1(A[24]), .out(S[25]), .sel(shift));
  Multiplexer multiplexer_27 (.in0(A[26]), .in1(A[25]), .out(S[26]), .sel(shift));
  Multiplexer multiplexer_28 (.in0(A[27]), .in1(A[26]), .out(S[27]), .sel(shift));
  Multiplexer multiplexer_29 (.in0(A[28]), .in1(A[27]), .out(S[28]), .sel(shift));
  Multiplexer multiplexer_30 (.in0(A[29]), .in1(A[28]), .out(S[29]), .sel(shift));
  Multiplexer multiplexer_31 (.in0(A[30]), .in1(A[29]), .out(S[30]), .sel(shift));
  Multiplexer multiplexer_32 (.in0(A[31]), .in1(A[30]), .out(S[31]), .sel(shift));
endmodule

module Shifter_4_bits (
  input  [31:0] A,
  input  shift,
  output [31:0] S
);

  Multiplexer multiplexer_1 (.in0(A[0]), .in1(1'b0), .out(S[0]), .sel(shift));
  Multiplexer multiplexer_2 (.in0(A[1]), .in1(1'b0), .out(S[1]), .sel(shift));
  Multiplexer multiplexer_3 (.in0(A[2]), .in1(1'b0), .out(S[2]), .sel(shift));
  Multiplexer multiplexer_4 (.in0(A[3]), .in1(1'b0), .out(S[3]), .sel(shift));
  Multiplexer multiplexer_5 (.in0(A[4]), .in1(A[0]), .out(S[4]), .sel(shift));
  Multiplexer multiplexer_6 (.in0(A[5]), .in1(A[1]), .out(S[5]), .sel(shift));
  Multiplexer multiplexer_7 (.in0(A[6]), .in1(A[2]), .out(S[6]), .sel(shift));
  Multiplexer multiplexer_8 (.in0(A[7]), .in1(A[3]), .out(S[7]), .sel(shift));
  Multiplexer multiplexer_9 (.in0(A[8]), .in1(A[4]), .out(S[8]), .sel(shift));
  Multiplexer multiplexer_10 (.in0(A[9]), .in1(A[5]), .out(S[9]), .sel(shift));
  Multiplexer multiplexer_11 (.in0(A[10]), .in1(A[6]), .out(S[10]), .sel(shift));
  Multiplexer multiplexer_12 (.in0(A[11]), .in1(A[7]), .out(S[11]), .sel(shift));
  Multiplexer multiplexer_13 (.in0(A[12]), .in1(A[8]), .out(S[12]), .sel(shift));
  Multiplexer multiplexer_14 (.in0(A[13]), .in1(A[9]), .out(S[13]), .sel(shift));
  Multiplexer multiplexer_15 (.in0(A[14]), .in1(A[10]), .out(S[14]), .sel(shift));
  Multiplexer multiplexer_16 (.in0(A[15]), .in1(A[11]), .out(S[15]), .sel(shift));
  Multiplexer multiplexer_17 (.in0(A[16]), .in1(A[12]), .out(S[16]), .sel(shift));
  Multiplexer multiplexer_18 (.in0(A[17]), .in1(A[13]), .out(S[17]), .sel(shift));
  Multiplexer multiplexer_19 (.in0(A[18]), .in1(A[14]), .out(S[18]), .sel(shift));
  Multiplexer multiplexer_20 (.in0(A[19]), .in1(A[15]), .out(S[19]), .sel(shift));
  Multiplexer multiplexer_21 (.in0(A[20]), .in1(A[16]), .out(S[20]), .sel(shift));
  Multiplexer multiplexer_22 (.in0(A[21]), .in1(A[17]), .out(S[21]), .sel(shift));
  Multiplexer multiplexer_23 (.in0(A[22]), .in1(A[18]), .out(S[22]), .sel(shift));
  Multiplexer multiplexer_24 (.in0(A[23]), .in1(A[19]), .out(S[23]), .sel(shift));
  Multiplexer multiplexer_25 (.in0(A[24]), .in1(A[20]), .out(S[24]), .sel(shift));
  Multiplexer multiplexer_26 (.in0(A[25]), .in1(A[21]), .out(S[25]), .sel(shift));
  Multiplexer multiplexer_27 (.in0(A[26]), .in1(A[22]), .out(S[26]), .sel(shift));
  Multiplexer multiplexer_28 (.in0(A[27]), .in1(A[23]), .out(S[27]), .sel(shift));
  Multiplexer multiplexer_29 (.in0(A[28]), .in1(A[24]), .out(S[28]), .sel(shift));
  Multiplexer multiplexer_30 (.in0(A[29]), .in1(A[25]), .out(S[29]), .sel(shift));
  Multiplexer multiplexer_31 (.in0(A[30]), .in1(A[26]), .out(S[30]), .sel(shift));
  Multiplexer multiplexer_32 (.in0(A[31]), .in1(A[27]), .out(S[31]), .sel(shift));
endmodule

module Shifter_8_bits (
  input  [31:0] A,
  input  shift,
  output [31:0] S
);

  Multiplexer multiplexer_1 (.in0(A[0]), .in1(1'b0), .out(S[0]), .sel(shift));
  Multiplexer multiplexer_2 (.in0(A[1]), .in1(1'b0), .out(S[1]), .sel(shift));
  Multiplexer multiplexer_3 (.in0(A[2]), .in1(1'b0), .out(S[2]), .sel(shift));
  Multiplexer multiplexer_4 (.in0(A[3]), .in1(1'b0), .out(S[3]), .sel(shift));
  Multiplexer multiplexer_5 (.in0(A[4]), .in1(1'b0), .out(S[4]), .sel(shift));
  Multiplexer multiplexer_6 (.in0(A[5]), .in1(1'b0), .out(S[5]), .sel(shift));
  Multiplexer multiplexer_7 (.in0(A[6]), .in1(1'b0), .out(S[6]), .sel(shift));
  Multiplexer multiplexer_8 (.in0(A[7]), .in1(1'b0), .out(S[7]), .sel(shift));
  Multiplexer multiplexer_9 (.in0(A[8]), .in1(A[0]), .out(S[8]), .sel(shift));
  Multiplexer multiplexer_10 (.in0(A[9]), .in1(A[1]), .out(S[9]), .sel(shift));
  Multiplexer multiplexer_11 (.in0(A[10]), .in1(A[2]), .out(S[10]), .sel(shift));
  Multiplexer multiplexer_12 (.in0(A[11]), .in1(A[3]), .out(S[11]), .sel(shift));
  Multiplexer multiplexer_13 (.in0(A[12]), .in1(A[4]), .out(S[12]), .sel(shift));
  Multiplexer multiplexer_14 (.in0(A[13]), .in1(A[5]), .out(S[13]), .sel(shift));
  Multiplexer multiplexer_15 (.in0(A[14]), .in1(A[6]), .out(S[14]), .sel(shift));
  Multiplexer multiplexer_16 (.in0(A[15]), .in1(A[7]), .out(S[15]), .sel(shift));
  Multiplexer multiplexer_17 (.in0(A[16]), .in1(A[8]), .out(S[16]), .sel(shift));
  Multiplexer multiplexer_18 (.in0(A[17]), .in1(A[9]), .out(S[17]), .sel(shift));
  Multiplexer multiplexer_19 (.in0(A[18]), .in1(A[10]), .out(S[18]), .sel(shift));
  Multiplexer multiplexer_20 (.in0(A[19]), .in1(A[11]), .out(S[19]), .sel(shift));
  Multiplexer multiplexer_21 (.in0(A[20]), .in1(A[12]), .out(S[20]), .sel(shift));
  Multiplexer multiplexer_22 (.in0(A[21]), .in1(A[13]), .out(S[21]), .sel(shift));
  Multiplexer multiplexer_23 (.in0(A[22]), .in1(A[14]), .out(S[22]), .sel(shift));
  Multiplexer multiplexer_24 (.in0(A[23]), .in1(A[15]), .out(S[23]), .sel(shift));
  Multiplexer multiplexer_25 (.in0(A[24]), .in1(A[16]), .out(S[24]), .sel(shift));
  Multiplexer multiplexer_26 (.in0(A[25]), .in1(A[17]), .out(S[25]), .sel(shift));
  Multiplexer multiplexer_27 (.in0(A[26]), .in1(A[18]), .out(S[26]), .sel(shift));
  Multiplexer multiplexer_28 (.in0(A[27]), .in1(A[19]), .out(S[27]), .sel(shift));
  Multiplexer multiplexer_29 (.in0(A[28]), .in1(A[20]), .out(S[28]), .sel(shift));
  Multiplexer multiplexer_30 (.in0(A[29]), .in1(A[21]), .out(S[29]), .sel(shift));
  Multiplexer multiplexer_31 (.in0(A[30]), .in1(A[22]), .out(S[30]), .sel(shift));
  Multiplexer multiplexer_32 (.in0(A[31]), .in1(A[23]), .out(S[31]), .sel(shift));
endmodule

module Shifter_16_bits (
  input  [31:0] A,
  input  shift,
  output [31:0] S
);

  Multiplexer multiplexer_1 (.in0(A[0]), .in1(1'b0), .out(S[0]), .sel(shift));
  Multiplexer multiplexer_2 (.in0(A[1]), .in1(1'b0), .out(S[1]), .sel(shift));
  Multiplexer multiplexer_3 (.in0(A[2]), .in1(1'b0), .out(S[2]), .sel(shift));
  Multiplexer multiplexer_4 (.in0(A[3]), .in1(1'b0), .out(S[3]), .sel(shift));
  Multiplexer multiplexer_5 (.in0(A[4]), .in1(1'b0), .out(S[4]), .sel(shift));
  Multiplexer multiplexer_6 (.in0(A[5]), .in1(1'b0), .out(S[5]), .sel(shift));
  Multiplexer multiplexer_7 (.in0(A[6]), .in1(1'b0), .out(S[6]), .sel(shift));
  Multiplexer multiplexer_8 (.in0(A[7]), .in1(1'b0), .out(S[7]), .sel(shift));
  Multiplexer multiplexer_9 (.in0(A[8]), .in1(1'b0), .out(S[8]), .sel(shift));
  Multiplexer multiplexer_10 (.in0(A[9]), .in1(1'b0), .out(S[9]), .sel(shift));
  Multiplexer multiplexer_11 (.in0(A[10]), .in1(1'b0), .out(S[10]), .sel(shift));
  Multiplexer multiplexer_12 (.in0(A[11]), .in1(1'b0), .out(S[11]), .sel(shift));
  Multiplexer multiplexer_13 (.in0(A[12]), .in1(1'b0), .out(S[12]), .sel(shift));
  Multiplexer multiplexer_14 (.in0(A[13]), .in1(1'b0), .out(S[13]), .sel(shift));
  Multiplexer multiplexer_15 (.in0(A[14]), .in1(1'b0), .out(S[14]), .sel(shift));
  Multiplexer multiplexer_16 (.in0(A[15]), .in1(1'b0), .out(S[15]), .sel(shift));
  Multiplexer multiplexer_17 (.in0(A[16]), .in1(A[1]), .out(S[16]), .sel(shift));
  Multiplexer multiplexer_18 (.in0(A[17]), .in1(A[2]), .out(S[17]), .sel(shift));
  Multiplexer multiplexer_19 (.in0(A[18]), .in1(A[3]), .out(S[18]), .sel(shift));
  Multiplexer multiplexer_20 (.in0(A[19]), .in1(A[4]), .out(S[19]), .sel(shift));
  Multiplexer multiplexer_21 (.in0(A[20]), .in1(A[5]), .out(S[20]), .sel(shift));
  Multiplexer multiplexer_22 (.in0(A[21]), .in1(A[6]), .out(S[21]), .sel(shift));
  Multiplexer multiplexer_23 (.in0(A[22]), .in1(A[7]), .out(S[22]), .sel(shift));
  Multiplexer multiplexer_24 (.in0(A[23]), .in1(A[8]), .out(S[23]), .sel(shift));
  Multiplexer multiplexer_25 (.in0(A[24]), .in1(A[9]), .out(S[24]), .sel(shift));
  Multiplexer multiplexer_26 (.in0(A[25]), .in1(A[10]), .out(S[25]), .sel(shift));
  Multiplexer multiplexer_27 (.in0(A[26]), .in1(A[11]), .out(S[26]), .sel(shift));
  Multiplexer multiplexer_28 (.in0(A[27]), .in1(A[12]), .out(S[27]), .sel(shift));
  Multiplexer multiplexer_29 (.in0(A[28]), .in1(A[13]), .out(S[28]), .sel(shift));
  Multiplexer multiplexer_30 (.in0(A[29]), .in1(A[14]), .out(S[29]), .sel(shift));
  Multiplexer multiplexer_31 (.in0(A[30]), .in1(A[15]), .out(S[30]), .sel(shift));
  Multiplexer multiplexer_32 (.in0(A[31]), .in1(A[16]), .out(S[31]), .sel(shift));
endmodule

module Shifter_32_bits (
  input  [31:0] A,
  input  [31:0] Shift,
  output [31:0] S
);

  wire or_1_out;
  wire [31:0] shifter_1_bit_1_s, shifter_2_bits_1_s, shifter_4_bits_1_s, shifter_8_bits_1_s,
       shifter_16_bits_1_s;

  Shifter_1_bit shifter_1_bit_1 (.A(A), .shift(Shift[0]), .S(shifter_1_bit_1_s));
  or or_1 (or_1_out, Shift[5], Shift[6], Shift[7], Shift[8], Shift[9], Shift[10], Shift[11], Shift[12], Shift[13], Shift[14], Shift[15], Shift[16], Shift[17], Shift[18], Shift[19], Shift[20], Shift[21], Shift[22], Shift[23], Shift[24], Shift[25], Shift[26], Shift[27], Shift[28], Shift[29], Shift[30], Shift[31]);
  Shifter_2_bits shifter_2_bits_1 (.A(shifter_1_bit_1_s), .shift(Shift[1]), .S(shifter_2_bits_1_s));
  Shifter_4_bits shifter_4_bits_1 (.A(shifter_2_bits_1_s), .shift(Shift[2]), .S(shifter_4_bits_1_s));
  Shifter_8_bits shifter_8_bits_1 (.A(shifter_4_bits_1_s), .shift(Shift[3]), .S(shifter_8_bits_1_s));
  Shifter_16_bits shifter_16_bits_1 (.A(shifter_8_bits_1_s), .shift(Shift[4]), .S(shifter_16_bits_1_s));
  Multiplexer #(.width(32)) multiplexer_1 (.in0(shifter_16_bits_1_s), .in1({32{1'b0}}), .out(S), .sel(or_1_out));
endmodule

module Zero_detector_32_bits (
  input  [31:0] in_1,
  output out_2
);

  nor nor_1 (out_2, in_1[0], in_1[1], in_1[2], in_1[3], in_1[4], in_1[5], in_1[6], in_1[7], in_1[8], in_1[9], in_1[10], in_1[11], in_1[12], in_1[13], in_1[14], in_1[16], in_1[17], in_1[18], in_1[19], in_1[20], in_1[21], in_1[22], in_1[23], in_1[24], in_1[25], in_1[26], in_1[27], in_1[28], in_1[29], in_1[30], in_1[31]);
endmodule

module ULA (
  input  [31:0] A,
  input  [31:0] B,
  input  [2:0] Funct,
  output ZERO,
  output [31:0] S
);

  wire [31:0] and_1_out, multiplexer_1_out, multiplier_1_out, not_1_out, or_1_out, shifter_32_bits_1_s,
       somador_32_bits_1_s, xor_1_out;

  Multiplexer #(.width(32)) multiplexer_1 (.in0(B), .in1(not_1_out), .out(multiplexer_1_out), .sel(Funct[0]));
  assign not_1_out = ~B;  // NOT_Gate not_1, 32 bits wide
  Somador_32_bits somador_32_bits_1 (
    .A(A), .B(multiplexer_1_out), .C_in(Funct[0]), .S(somador_32_bits_1_s));  // open: Overflow
  Multiplier #(.width(32)) multiplier_1 (.a(A), .b(B), .out(multiplier_1_out));  // open: cin, cout
  assign and_1_out = A & B;  // AND_Gate and_1, 32 bits wide
  assign or_1_out = A | B;  // OR_Gate or_1, 32 bits wide
  assign xor_1_out = A ^ B;  // XOR_Gate xor_1, 32 bits wide
  Shifter_32_bits shifter_32_bits_1 (.A(A), .Shift(B), .S(shifter_32_bits_1_s));
  Zero_detector_32_bits zero_detector_32_bits_1 (.in_1(S), .out_2(ZERO));
  Multiplexer #(.select(3), .width(32)) multiplexer_2 (
    .in0(somador_32_bits_1_s), .in1(somador_32_bits_1_s), .in2(multiplier_1_out), .in3(and_1_out),
    .in4(or_1_out), .in5(xor_1_out), .in6(shifter_32_bits_1_s), .out(S), .sel(Funct));  // open: in7
endmodule
