// Logisim project trab1grr20243764.circ as structural Verilog: 15 circuits, main circuit main
module main (
  input  [3:0] in_1,
  input  [3:0] in_2,
  input  [2:0] in_3
);

  wire ula_1_p8;
  wire [3:0] undriven;

  // ULA ula_1: pin names not known; wires that end beside it: in_1[1], in_1[2], in_1[3], in_2[0], in_2[1], in_2[2], in_2[3], ula_1_p8, undriven[1], undriven[2], undriven[3], in_3[0], in_3[1], in_3[2]
  // Probe on ula_1_p8
  // Probe on undriven

  // Notes on the sheet:
  //   Teste A
  //   Teste B
  //   Teste Seletor
  //   NAO MODIFIQUE ESTE CIRCUITO NEM OS FIOS DE TESTE
  //   Saida F
  //   Saida R
endmodule

module ULA (
  input  B0,
  input  A0,
  input  B1,
  input  A1,
  input  B2,
  input  A2,
  input  B3,
  input  A3,
  input  S2,
  input  S1,
  input  S0,
  output F,
  output R0,
  output R1,
  output R2,
  output R3
);

  wire \andab_1_saída_r , \andab_2_saída_r , \andab_3_saída_r , \inversoa_1_saída_r__a_prime ,
       \inversoa_2_saída_r__a_prime , \inversoa_3_saída_r__a_prime , \inversoa_4_saída_r__a_prime ,
       \orab_1_saída_r , \orab_2_saída_r , \orab_3_saída_r , \orab_4_saída_r , \orab_5_saída_r ,
       shiftleft_1_out_9, shiftleft_1_out_10, shiftleft_1_out_11, shiftleft_1_out_12, shiftright_1_out_9,
       shiftright_1_out_10, shiftright_1_out_11, shiftright_1_out_12, somador_1_out_9, somador_1_out_10,
       somador_1_out_11, somador_1_out_12, somador_1_out_13, subtrator_1_out_9, subtrator_1_out_10,
       subtrator_1_out_11, subtrator_1_out_12, subtrator_1_out_13, \xorab_1_saída_r , \xorab_2_saída_r ,
       \xorab_3_saída_r , \xorab_4_saída_r ;

  Somador somador_1 (
    .out_9(somador_1_out_9), .in_1(A3), .in_2(B3), .in_3(A2), .in_4(B2), .in_5(A1), .in_6(B1), .in_7(A0),
    .in_8(B0), .out_10(somador_1_out_10), .out_11(somador_1_out_11), .out_12(somador_1_out_12),
    .out_13(somador_1_out_13));
  Subtrator subtrator_1 (
    .out_9(subtrator_1_out_9), .in_1(A3), .in_2(B3), .in_3(A2), .in_4(B2), .in_5(A1), .in_6(B1), .in_7(A0),
    .in_8(B0), .out_10(subtrator_1_out_10), .out_11(subtrator_1_out_11), .out_12(subtrator_1_out_12),
    .out_13(subtrator_1_out_13));
  ShiftLeft shiftleft_1 (
    .A0(A0), .A1(A1), .A2(A2), .A3(A3), .B0(B0), .B1(B1), .B2(B2), .B3(B3), .out_9(shiftleft_1_out_9),
    .out_10(shiftleft_1_out_10), .out_11(shiftleft_1_out_11), .out_12(shiftleft_1_out_12));
  ShiftRight shiftright_1 (
    .A0(A0), .A1(A1), .A2(A2), .A3(A3), .B0(B0), .in_6(B1), .in_7(B2), .in_8(B3), .out_9(shiftright_1_out_9),
    .out_10(shiftright_1_out_10), .out_11(shiftright_1_out_11), .out_12(shiftright_1_out_12));
  AndAB andab_1 (.A(B0), .B(A0), .\Saída_R (\andab_1_saída_r ));
  OrAB orab_1 (.A(B1), .B(A1), .\Saída_R (\orab_1_saída_r ));
  AndAB andab_2 (.A(B2), .B(A2), .\Saída_R (\andab_2_saída_r ));
  AndAB andab_3 (.A(B3), .B(A3), .\Saída_R (\andab_3_saída_r ));
  OrAB orab_2 (.A(B0), .B(A0), .\Saída_R (\orab_2_saída_r ));
  OrAB orab_3 (.A(B1), .B(A1), .\Saída_R (\orab_3_saída_r ));
  OrAB orab_4 (.A(B2), .B(A2), .\Saída_R (\orab_4_saída_r ));
  OrAB orab_5 (.A(B3), .B(A3), .\Saída_R (\orab_5_saída_r ));
  InversoA inversoa_1 (.A(A0), .\Saída_R__A_prime (\inversoa_1_saída_r__a_prime ));
  InversoA inversoa_2 (.A(A1), .\Saída_R__A_prime (\inversoa_2_saída_r__a_prime ));
  InversoA inversoa_3 (.A(A2), .\Saída_R__A_prime (\inversoa_3_saída_r__a_prime ));
  InversoA inversoa_4 (.A(A3), .\Saída_R__A_prime (\inversoa_4_saída_r__a_prime ));
  XorAB xorab_1 (.A(B0), .B(A0), .\Saída_R (\xorab_1_saída_r ));
  XorAB xorab_2 (.A(B1), .B(A1), .\Saída_R (\xorab_2_saída_r ));
  XorAB xorab_3 (.A(B2), .B(A2), .\Saída_R (\xorab_3_saída_r ));
  XorAB xorab_4 (.A(B3), .B(A3), .\Saída_R (\xorab_4_saída_r ));
  OrAB orab_6 (.A(subtrator_1_out_9), .B(somador_1_out_9), .\Saída_R (F));
  MultiplexadorDe3Seletores multiplexadorde3seletores_1 (
    .E0(somador_1_out_13), .E1(subtrator_1_out_13), .E2(shiftleft_1_out_9), .E3(shiftright_1_out_9),
    .E4(\andab_1_saída_r ), .E5(\orab_2_saída_r ), .E6(\inversoa_1_saída_r__a_prime ),
    .E7(\xorab_1_saída_r ), .S2(S2), .in_10(S1), .in_11(S0), .out_12(R0));
  MultiplexadorDe3Seletores multiplexadorde3seletores_2 (
    .E0(somador_1_out_12), .E1(subtrator_1_out_12), .E2(shiftleft_1_out_10), .E3(shiftright_1_out_10),
    .E4(\orab_1_saída_r ), .E5(\orab_3_saída_r ), .E6(\inversoa_2_saída_r__a_prime ), .E7(\xorab_2_saída_r ),
    .S2(S2), .in_10(S1), .in_11(S0), .out_12(R1));
  MultiplexadorDe3Seletores multiplexadorde3seletores_3 (
    .E0(somador_1_out_11), .E1(subtrator_1_out_11), .E2(shiftleft_1_out_11), .E3(shiftright_1_out_11),
    .E4(\andab_2_saída_r ), .E5(\orab_4_saída_r ), .E6(\inversoa_3_saída_r__a_prime ),
    .E7(\xorab_3_saída_r ), .S2(S2), .in_10(S1), .in_11(S0), .out_12(R2));
  MultiplexadorDe3Seletores multiplexadorde3seletores_4 (
    .E0(somador_1_out_10), .E1(subtrator_1_out_10), .E2(shiftleft_1_out_12), .E3(shiftright_1_out_12),
    .E4(\andab_3_saída_r ), .E5(\orab_5_saída_r ), .E6(\inversoa_4_saída_r__a_prime ),
    .E7(\xorab_4_saída_r ), .S2(S2), .in_10(S1), .in_11(S0), .out_12(R3));

  // Notes on the sheet:
  //   SOMADOR
  //   SUBTRATOR
  //   SHIFT LEFT
  //   SHIFT RIGHT
  //   AND
  //   OR
  //   A'
  //   XOR
  //   SE 1 É OVERFLOW, SE 0 NÃO
  //   MUX
  //   MUX
  //   MUX
  //   MUX
endmodule

module Somador (
  input  in_1,
  input  in_2,
  input  in_3,
  input  in_4,
  input  in_5,
  input  in_6,
  input  in_7,
  input  in_8,
  output out_9,
  output out_10,
  output out_11,
  output out_12,
  output out_13
);

  wire fulladder_2_out_4, fulladder_3_out_4, halfadder_1_out_3;

  FullAdder fulladder_1 (.out_4(out_9), .in_1(in_1), .in_2(in_2), .out_5(out_10), .Vem_Um(fulladder_2_out_4));
  FullAdder fulladder_2 (
    .out_4(fulladder_2_out_4), .in_1(in_3), .in_2(in_4), .out_5(out_11), .Vem_Um(fulladder_3_out_4));
  FullAdder fulladder_3 (
    .out_4(fulladder_3_out_4), .in_1(in_5), .in_2(in_6), .out_5(out_12), .Vem_Um(halfadder_1_out_3));
  HalfAdder halfadder_1 (.out_3(halfadder_1_out_3), .in_1(in_7), .in_2(in_8), .out_4(out_13));

  // Notes on the sheet:
  //   Se 1 é overflow,se 0, não
  //   A3,B3
  //   A2,B2
  //   A1,B1
  //   Saída dos Bits
  //   A0,B0
endmodule

module Subtrator (
  input  in_1,
  input  in_2,
  input  in_3,
  input  in_4,
  input  in_5,
  input  in_6,
  input  in_7,
  input  in_8,
  output out_9,
  output out_10,
  output out_11,
  output out_12,
  output out_13
);

  wire fulladderinvertido_2_out_4, fulladderinvertido_3_out_4, fulladderinvertido_4_out_4;

  FullAdderInvertido fulladderinvertido_1 (
    .out_4(out_9), .A(in_1), .in_2(in_2), .out_5(out_10), .plus_1(fulladderinvertido_2_out_4));
  FullAdderInvertido fulladderinvertido_2 (
    .out_4(fulladderinvertido_2_out_4), .A(in_3), .in_2(in_4), .out_5(out_11),
    .plus_1(fulladderinvertido_3_out_4));
  FullAdderInvertido fulladderinvertido_3 (
    .out_4(fulladderinvertido_3_out_4), .A(in_5), .in_2(in_6), .out_5(out_12),
    .plus_1(fulladderinvertido_4_out_4));
  FullAdderInvertido fulladderinvertido_4 (
    .out_4(fulladderinvertido_4_out_4), .A(in_7), .in_2(in_8), .out_5(out_13), .plus_1(1'b1));

  // Notes on the sheet:
  //   Saída se 1 overflow, se 0, não
  //   A3,B3
  //   A2,B2
  //   Saída dos bits
  //   A1,B1
  //   A0,B0
endmodule

module HalfAdder (
  input  in_1,
  input  in_2,
  output out_3,
  output out_4
);

  and and_1 (out_3, in_1, in_2);
  xor xor_1 (out_4, in_1, in_2);

  // Notes on the sheet:
  //   Saída para o "vai um"
  //   A
  //   B
  //   Saída do Bit
endmodule

module FullAdder (
  input  in_1,
  input  in_2,
  input  Vem_Um,
  output out_4,
  output out_5
);

  wire and_1_out, and_2_out, or_2_out;

  or or_1 (out_4, and_2_out, and_1_out);
  and and_1 (and_1_out, Vem_Um, or_2_out);
  and and_2 (and_2_out, in_1, in_2);
  or or_2 (or_2_out, in_1, in_2);
  ExactlyOne xor_1 (.out(out_5), .in0(in_1), .in1(Vem_Um), .in2(in_2));

  // Notes on the sheet:
  //   Saída para o "vai um"
  //   A
  //   B
  //   Saída do Bit
endmodule

module FullAdderInvertido (
  input  A,
  input  in_2,
  input  plus_1,
  output out_4,
  output out_5
);

  wire and_1_out, and_2_out, not_1_out, or_2_out;

  or or_1 (out_4, and_2_out, and_1_out);
  and and_1 (and_1_out, plus_1, or_2_out);
  and and_2 (and_2_out, A, not_1_out);
  or or_2 (or_2_out, A, not_1_out);
  ExactlyOne xor_1 (.out(out_5), .in0(A), .in1(plus_1), .in2(not_1_out));
  not not_1 (not_1_out, in_2);

  // Notes on the sheet:
  //   Saída para o "vai um"
  //   B
  //   Saída para o Bit
endmodule

module ShiftLeft (
  input  A0,
  input  A1,
  input  A2,
  input  A3,
  input  B0,
  input  B1,
  input  B2,
  input  B3,
  output out_9,
  output out_10,
  output out_11,
  output out_12
);

  wire multiplexadorde1seletor_1_out_4, multiplexadorde1seletor_2_out_4, multiplexadorde1seletor_3_out_4,
       multiplexadorde1seletor_4_out_4, multiplexadorde1seletor_5_out_4, multiplexadorde1seletor_6_out_4,
       multiplexadorde1seletor_7_out_4, multiplexadorde1seletor_8_out_4, multiplexadorde1seletor_9_out_4,
       multiplexadorde1seletor_10_out_4, multiplexadorde1seletor_11_out_4, multiplexadorde1seletor_12_out_4;

  MultiplexadorDe1Seletor multiplexadorde1seletor_1 (
    .E0(A0), .E1(A1), .in_3(B0), .out_4(multiplexadorde1seletor_1_out_4));
  MultiplexadorDe1Seletor multiplexadorde1seletor_2 (
    .E0(A1), .E1(A2), .in_3(B0), .out_4(multiplexadorde1seletor_2_out_4));
  MultiplexadorDe1Seletor multiplexadorde1seletor_3 (
    .E0(A2), .E1(A3), .in_3(B0), .out_4(multiplexadorde1seletor_3_out_4));
  MultiplexadorDe1Seletor multiplexadorde1seletor_4 (
    .E0(A3), .E1(1'b0), .in_3(B0), .out_4(multiplexadorde1seletor_4_out_4));
  MultiplexadorDe1Seletor multiplexadorde1seletor_5 (
    .E0(multiplexadorde1seletor_1_out_4), .E1(multiplexadorde1seletor_3_out_4), .in_3(B1),
    .out_4(multiplexadorde1seletor_5_out_4));
  MultiplexadorDe1Seletor multiplexadorde1seletor_6 (
    .E0(multiplexadorde1seletor_2_out_4), .E1(multiplexadorde1seletor_4_out_4), .in_3(B1),
    .out_4(multiplexadorde1seletor_6_out_4));
  MultiplexadorDe1Seletor multiplexadorde1seletor_7 (
    .E0(multiplexadorde1seletor_3_out_4), .E1(1'b0), .in_3(B1), .out_4(multiplexadorde1seletor_7_out_4));
  MultiplexadorDe1Seletor multiplexadorde1seletor_8 (
    .E0(multiplexadorde1seletor_4_out_4), .E1(1'b0), .in_3(B1), .out_4(multiplexadorde1seletor_8_out_4));
  MultiplexadorDe1Seletor multiplexadorde1seletor_9 (
    .E0(multiplexadorde1seletor_5_out_4), .E1(1'b0), .in_3(B2), .out_4(multiplexadorde1seletor_9_out_4));
  MultiplexadorDe1Seletor multiplexadorde1seletor_10 (
    .E0(multiplexadorde1seletor_6_out_4), .E1(1'b0), .in_3(B2), .out_4(multiplexadorde1seletor_10_out_4));
  MultiplexadorDe1Seletor multiplexadorde1seletor_11 (
    .E0(multiplexadorde1seletor_7_out_4), .E1(1'b0), .in_3(B2), .out_4(multiplexadorde1seletor_11_out_4));
  MultiplexadorDe1Seletor multiplexadorde1seletor_12 (
    .E0(multiplexadorde1seletor_8_out_4), .E1(1'b0), .in_3(B2), .out_4(multiplexadorde1seletor_12_out_4));
  MultiplexadorDe1Seletor multiplexadorde1seletor_13 (
    .E0(multiplexadorde1seletor_9_out_4), .E1(1'b0), .in_3(B3), .out_4(out_9));
  MultiplexadorDe1Seletor multiplexadorde1seletor_14 (
    .E0(multiplexadorde1seletor_10_out_4), .E1(1'b0), .in_3(B3), .out_4(out_10));
  MultiplexadorDe1Seletor multiplexadorde1seletor_15 (
    .E0(multiplexadorde1seletor_11_out_4), .E1(1'b0), .in_3(B3), .out_4(out_11));
  MultiplexadorDe1Seletor multiplexadorde1seletor_16 (
    .E0(multiplexadorde1seletor_12_out_4), .E1(1'b0), .in_3(B3), .out_4(out_12));
endmodule

module ShiftRight (
  input  A0,
  input  A1,
  input  A2,
  input  A3,
  input  B0,
  input  in_6,
  input  in_7,
  input  in_8,
  output out_9,
  output out_10,
  output out_11,
  output out_12
);

  wire multiplexadorde1seletor_1_out_4, multiplexadorde1seletor_2_out_4, multiplexadorde1seletor_3_out_4,
       multiplexadorde1seletor_4_out_4, multiplexadorde1seletor_5_out_4, multiplexadorde1seletor_6_out_4,
       multiplexadorde1seletor_7_out_4, multiplexadorde1seletor_8_out_4, multiplexadorde1seletor_9_out_4,
       multiplexadorde1seletor_10_out_4, multiplexadorde1seletor_11_out_4, multiplexadorde1seletor_12_out_4;

  MultiplexadorDe1Seletor multiplexadorde1seletor_1 (
    .E0(A0), .E1(1'b0), .in_3(B0), .out_4(multiplexadorde1seletor_1_out_4));
  MultiplexadorDe1Seletor multiplexadorde1seletor_2 (
    .E0(A1), .E1(A0), .in_3(B0), .out_4(multiplexadorde1seletor_2_out_4));
  MultiplexadorDe1Seletor multiplexadorde1seletor_3 (
    .E0(A2), .E1(A1), .in_3(B0), .out_4(multiplexadorde1seletor_3_out_4));
  MultiplexadorDe1Seletor multiplexadorde1seletor_4 (
    .E0(A3), .E1(A2), .in_3(B0), .out_4(multiplexadorde1seletor_4_out_4));
  MultiplexadorDe1Seletor multiplexadorde1seletor_5 (
    .E0(multiplexadorde1seletor_1_out_4), .E1(1'b0), .in_3(in_6), .out_4(multiplexadorde1seletor_5_out_4));
  MultiplexadorDe1Seletor multiplexadorde1seletor_6 (
    .E0(multiplexadorde1seletor_2_out_4), .E1(1'b0), .in_3(in_6), .out_4(multiplexadorde1seletor_6_out_4));
  MultiplexadorDe1Seletor multiplexadorde1seletor_7 (
    .E0(multiplexadorde1seletor_3_out_4), .E1(multiplexadorde1seletor_1_out_4), .in_3(in_6),
    .out_4(multiplexadorde1seletor_7_out_4));
  MultiplexadorDe1Seletor multiplexadorde1seletor_8 (
    .E0(multiplexadorde1seletor_4_out_4), .E1(multiplexadorde1seletor_2_out_4), .in_3(in_6),
    .out_4(multiplexadorde1seletor_8_out_4));
  MultiplexadorDe1Seletor multiplexadorde1seletor_9 (
    .E0(multiplexadorde1seletor_5_out_4), .E1(1'b0), .in_3(in_7), .out_4(multiplexadorde1seletor_9_out_4));
  MultiplexadorDe1Seletor multiplexadorde1seletor_10 (
    .E0(multiplexadorde1seletor_6_out_4), .E1(1'b0), .in_3(in_7), .out_4(multiplexadorde1seletor_10_out_4));
  MultiplexadorDe1Seletor multiplexadorde1seletor_11 (
    .E0(multiplexadorde1seletor_7_out_4), .E1(1'b0), .in_3(in_7), .out_4(multiplexadorde1seletor_11_out_4));
  MultiplexadorDe1Seletor multiplexadorde1seletor_12 (
    .E0(multiplexadorde1seletor_8_out_4), .E1(multiplexadorde1seletor_5_out_4), .in_3(in_7),
    .out_4(multiplexadorde1seletor_12_out_4));
  MultiplexadorDe1Seletor multiplexadorde1seletor_13 (
    .E0(multiplexadorde1seletor_9_out_4), .E1(1'b0), .in_3(in_8), .out_4(out_9));
  MultiplexadorDe1Seletor multiplexadorde1seletor_14 (
    .E0(multiplexadorde1seletor_10_out_4), .E1(1'b0), .in_3(in_8), .out_4(out_10));
  MultiplexadorDe1Seletor multiplexadorde1seletor_15 (
    .E0(multiplexadorde1seletor_11_out_4), .E1(1'b0), .in_3(in_8), .out_4(out_11));
  MultiplexadorDe1Seletor multiplexadorde1seletor_16 (
    .E0(multiplexadorde1seletor_12_out_4), .E1(1'b0), .in_3(in_8), .out_4(out_12));

  // Notes on the sheet:
  //   B1
  //   B2
  //   B3
endmodule

module MultiplexadorDe1Seletor (
  input  E0,
  input  E1,
  input  in_3,
  output out_4
);

  wire and_1_out, and_2_out;

  and and_1 (and_1_out, E0, ~in_3);  // AND_Gate
  and and_2 (and_2_out, E1, in_3);
  or or_1 (out_4, and_1_out, and_2_out);

  // Notes on the sheet:
  //   S0
endmodule

module MultiplexadorDe3Seletores (
  input  E0,
  input  E1,
  input  E2,
  input  E3,
  input  E4,
  input  E5,
  input  E6,
  input  E7,
  input  S2,
  input  in_10,
  input  in_11,
  output out_12
);

  wire and_1_out, and_2_out, and_3_out, and_4_out, and_5_out, and_6_out, and_7_out, and_8_out;

  and and_1 (and_1_out, ~E0, ~S2, ~in_10, ~in_11);  // AND_Gate
  and and_2 (and_2_out, ~E1, ~S2, ~in_10, in_11);  // AND_Gate
  and and_3 (and_3_out, ~E2, ~S2, in_10, ~in_11);  // AND_Gate
  and and_4 (and_4_out, ~E3, ~S2, in_10, in_11);  // AND_Gate
  and and_5 (and_5_out, ~E4, S2, ~in_10, ~in_11);  // AND_Gate
  and and_6 (and_6_out, ~E5, S2, ~in_10, in_11);  // AND_Gate
  and and_7 (and_7_out, ~E6, S2, in_10, ~in_11);  // AND_Gate
  and and_8 (and_8_out, ~E7, S2, in_10, in_11);  // AND_Gate
  or or_1 (out_12, and_1_out, and_2_out, and_3_out, and_4_out, and_5_out, and_6_out, and_7_out, and_8_out);

  // Notes on the sheet:
  //   S1
  //   S0
endmodule

module AndAB (
  input  A,
  input  B,
  output \Saída_R 
);

  and and_1 (\Saída_R , A, B);
endmodule

module OrAB (
  input  A,
  input  B,
  output \Saída_R 
);

  or or_1 (\Saída_R , A, B);
endmodule

module InversoA (
  input  A,
  output \Saída_R__A_prime 
);

  not not_1 (\Saída_R__A_prime , A);
endmodule

module XorAB (
  input  A,
  input  B,
  output \Saída_R 
);

  xor xor_1 (\Saída_R , A, B);
endmodule
